# Fritzing sketch ArtemisAtpSpeechControledLevel (saved by Fritzing 0.9.3b)
breadboards: 1

parts:
  SparkFun_RedBoard_Artemis_ATP1 = SparkFun RedBoard Artemis ATP
  R1 = Resistor [tolerance=±5% resistance=120 package=THT]
  R2 = Resistor [tolerance=±5% resistance=120 package=THT]
  R3 = Resistor [tolerance=±5% resistance=120 package=THT]
  R4 = Resistor [tolerance=±5% resistance=120 package=THT]
  LED1 = LED - 5mm [color="Red (633nm)" package="5 mm [THT]"]
  LED2 = LED - 5mm [color="Red (633nm)" package="5 mm [THT]"]
  LED3 = LED - 5mm [color="Orange (620nm)" package="5 mm [THT]"]
  LED4 = LED - 5mm [color="Orange (620nm)" package="5 mm [THT]"]

nets:
  N1: SparkFun_RedBoard_Artemis_ATP1.GND, R1.Pin_0, R2.Pin_0, R3.Pin_0, R4.Pin_0
  N2: SparkFun_RedBoard_Artemis_ATP1.D9, LED4.anode
  N3: SparkFun_RedBoard_Artemis_ATP1.D10, LED3.anode
  N4: SparkFun_RedBoard_Artemis_ATP1.D8, LED2.anode
  N5: SparkFun_RedBoard_Artemis_ATP1.D14, LED1.anode
  N6: R1.Pin_1, LED4.cathode
  N7: R2.Pin_1, LED3.cathode
  N8: R3.Pin_1, LED2.cathode
  N9: R4.Pin_1, LED1.cathode

custom parts:
  SparkFun RedBoard Artemis ATP: The RedBoard Artemis ATP is affectionately called 'All the Pins!' at SparkFun. The Artemis module has 48 GPIO and this board breaks out absolutely every one of them in a familiar Mega like form factor. What's with the silkscreen labels? They're all over the place. We decided to label the pins as they are assigned on the Apollo3 IC itself. This makes finding the pin with the function you desire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
